# Fritzing sketch Projeto (saved by Fritzing 0.9.3b)
breadboards: 1

parts:
  Q1 = NPN-Transistor [package="TO92 [THT]"]
  R1 = Resistor [tolerance=±5% resistance=220 package=THT]
  LED1 = LEDs [package=led10mm]
  Componente1 = Arduino Uno (Rev3)
  DHT1 = DHT11 Humitidy and Temperature Sensor (3 pins)
  Mod1 = MQ-7 breakout
  Mod2 = zmpt101b
  Mod3 = zmpt101b
  Grove1 = Grove Dust Sensor
  Componente2 = Arduino Ethernet Shield (Rev3)
  LCD1 = LCD screen
  LCM1602_IIC1 = LCM1602 IIC [part_number="LCM1602 IIC" chip_label="LCM1602 IIC" package="DIP (Dual Inline) [THT]"]

nets:
  N1: Q1.E, LED1.C
  N2: Q1.B, R1.Pin_1
  GND: Q1.C, Componente1.GND, DHT1.GND, Mod1.GND, Mod2.GND#3, Mod3.GND#3, Grove1.GND, LCM1602_IIC1.GND
  N3: R1.Pin_0, Componente1.D3_PWM
  VCC: LED1.A, Componente1.5V, DHT1.VDD, Mod1.VCC, Mod2.VCC, Mod3.VCC, Grove1.VCC, LCM1602_IIC1.VCC
  N4: Componente1.A0, DHT1.DATA
  N5: Componente1.A1, Mod1.AO
  N6: Componente1.A2, Mod2.OUT
  N7: Componente1.A3, Mod3.OUT
  N8: Componente1.A4/SDA, Grove1.SIG, LCM1602_IIC1.SDA
  N9: Componente1.D10_PWM/SS, Componente2.ETH_CS
  N10: Componente1.D11_PWM/MOSI, Componente2.PWM_D11
  N11: Componente1.D12/MISO, Componente2.SPI/D12
  N12: Componente1.D13/SCK, Componente2.SPI/D13
  N13: Componente1.A5/SCL, LCM1602_IIC1.SCL
  N14: Componente1.D2, Grove1.NC
  VSS: LCD1.VSS, LCM1602_IIC1.VSS
  VDD: LCD1.VDD, LCM1602_IIC1.VDD
  N15: LCD1.V0, LCM1602_IIC1.V0
  N16: LCD1.RS, LCM1602_IIC1.RS
  N17: LCD1.R/W, LCM1602_IIC1.RW
  N18: LCD1.E, LCM1602_IIC1.E
  N19: LCD1.DB0, LCM1602_IIC1.D0
  N20: LCD1.DB1, LCM1602_IIC1.D1
  N21: LCD1.DB2, LCM1602_IIC1.D2
  N22: LCD1.DB3, LCM1602_IIC1.D3
  N23: LCD1.DB4, LCM1602_IIC1.D4
  N24: LCD1.DB5, LCM1602_IIC1.D5
  N25: LCD1.DB6, LCM1602_IIC1.D6
  N26: LCD1.DB7, LCM1602_IIC1.D7
  N27: LCD1.LED+, LCM1602_IIC1.A
  N28: LCD1.LED-, LCM1602_IIC1.K
  N29: LCM1602_IIC1.LED_A, LCM1602_IIC1.LED_B

notes:
  - / +
  Emissor infravermelho
  S / + / -
  dht11 ou 22
  VCC / GND / D0 / A0
  MQ-Variantes
  zmpt101b
  GND / GND / OUT / VCC
  dsn501a
  Controle (Vout1) / Vout2 / VCC / Vout1 / GND
  Transistor
  222A
  220Ω resistor ou até 150Ω para maior intensidade
  Importante:
  Transitor 2N2222 e resistor 470Ω são recomendados pelo projeto original

custom parts:
  DHT11 Humitidy and Temperature Sensor (3 pins): DHT11 Humidity and Temperature Sensor (3 pins) from the design created by John De Cristofaro for Adafruit Industries.
  MQ-7 breakout: MQ-5 gas sensor
  zmpt101b: Single phase ac active output voltate transformer module.
  Grove Dust Sensor: PPD42 Grove Dust Sensor
  LCM1602 IIC: I2C-Module to use a 1602 or 2004 LCD on with the wire.h libory Serial LCD Modul
